// Logisim project alu.circ as structural Verilog: 1 circuit, main circuit alu
module alu (
  input  [31:0] A,
  input  [31:0] B,
  input  [3:0] ALUSel,
  output [31:0] ALUResult
);

  wire SLT2;
  wire [31:0] add0, AND7, bit_extender_1_out, MUL8, MULH9, MULHU11, OR6, SLL1, SRA13, SRL5, SUB12, XOR4;

  Adder #(.width(32)) adder_1 (.a(A), .b(B), .out(add0));  // open: cin, cout
  Shifter #(.width(32)) shifter_1 (.in(A), .\dist (B[4:0]), .out(SLL1));
  Comparator #(.width(32)) comparator_1 (.a(A), .b(B), .lt(SLT2));  // open: gt, eq
  assign XOR4 = A ^ B;  // XOR_Gate xor_1, 32 bits wide
  Shifter #(.shift("lr"), .width(32)) shifter_2 (.in(A), .\dist (B[4:0]), .out(SRL5));
  assign OR6 = A | B;  // OR_Gate or_1, 32 bits wide
  assign AND7 = A & B;  // AND_Gate and_1, 32 bits wide
  Multiplier #(.mode("twosComplement"), .width(32)) multiplier_1 (.a(A), .b(B), .out(MUL8), .cout(MULH9));  // open: cin
  Multiplier #(.width(32)) multiplier_2 (.a(A), .b(B), .cout(MULHU11));  // open: out, cin
  Subtractor #(.width(32)) subtractor_1 (.a(A), .b(B), .out(SUB12));  // open: bin, bout
  Shifter #(.shift("ar"), .width(32)) shifter_3 (.in(A), .\dist (B[4:0]), .out(SRA13));
  assign bit_extender_1_out = {{31{1'b0}}, SLT2};  // Bit_Extender bit_extender_1
  Multiplexer #(.enable("false"), .select(4), .width(32)) multiplexer_1 (
    .in0(add0), .in1(SLL1), .in2(bit_extender_1_out), .in3({32{1'b0}}), .in4(XOR4), .in5(SRL5), .in6(OR6),
    .in7(AND7), .in8(MUL8), .in9(MULH9), .in10({32{1'b0}}), .in11(MULHU11), .in12(SUB12), .in13(SRA13),
    .in14({32{1'b0}}), .in15(B), .out(ALUResult), .sel(ALUSel));

  // Other names for the same wires on the sheet: BSEL[31:0] = B

  // Notes on the sheet:
  //   INPUTS to your circuit
  //   DON'T CHANGE THE LOCATIONS OF THE INPUTS AND OUTPUTS!
  //   OUTPUT from your circuit
endmodule
