// Logisim project control-logic.circ as structural Verilog: 1 circuit, main circuit control_logic
module control_logic (
  input  [31:0] Instruction,
  input  BrEq,
  input  BrLt,
  output PCSel,
  output RegWEn,
  output [2:0] ImmSel,
  output BrUn,
  output ASel,
  output BSel,
  output [3:0] ALUSel,
  output MemWEn,
  output [1:0] WBSel
);

  wire add, addi, and11, andi, auipc, b0000000, b0000001, b0100000, beq, bge, bgeu, blt, bltu, bne, c1, c2,
       c3, c4, c5, c6, c7, c8, comparator_1_eq, comparator_11_eq, comparator_12_eq, demultiplexer_3_out1,
       demultiplexer_3_out5, IMM, jal, jalr, JMP, lb, lh, LOAD, lui, lw, mul, mulh, mulhu, not_1_out,
       not_2_out, not_3_out, or10, or_2_out, or_3_out, ori, p0, p1, p2, p3, p4, p5, p6, p7, sb, sh, sll3,
       slli, slt, slti, sra9, srai, srl8, srli, STORE, sub, sw, xor7, xori;
  wire [1:0] priority_encoder_1_en_out;
  wire [2:0] priority_encoder_2_out;
  wire [4:0] priority_encoder_1_out;
  wire [5:0] adder_1_out, bit_extender_1_out, bit_extender_2_out, input0;
  wire [15:14] rom_1_data;

  ROM #(.addrWidth(6), .dataWidth(16)) rom_1 (
    .addr(input0), .data({rom_1_data, WBSel, MemWEn, ALUSel, BSel, ASel, BrUn, ImmSel, RegWEn}));
  Comparator #(.width(7)) comparator_1 (.a(Instruction[6:0]), .b(7'b0110011), .eq(comparator_1_eq));  // open: gt, lt
  Comparator #(.width(7)) comparator_2 (.a(Instruction[6:0]), .b(7'b0000011), .eq(LOAD));  // open: gt, lt
  Comparator #(.width(7)) comparator_3 (.a(Instruction[6:0]), .b(7'b0010011), .eq(IMM));  // open: gt, lt
  Comparator #(.width(7)) comparator_4 (.a(Instruction[6:0]), .b(7'b0100011), .eq(STORE));  // open: gt, lt
  Comparator #(.width(7)) comparator_5 (.a(Instruction[6:0]), .b(7'b1100011), .eq(JMP));  // open: gt, lt
  Comparator #(.width(7)) comparator_6 (.a(Instruction[6:0]), .b(7'b0010111), .eq(auipc));  // open: gt, lt
  Comparator #(.width(7)) comparator_7 (.a(Instruction[6:0]), .b(7'b0110111), .eq(lui));  // open: gt, lt
  Comparator #(.width(7)) comparator_8 (.a(Instruction[6:0]), .b(7'b1101111), .eq(jal));  // open: gt, lt
  Comparator #(.width(7)) comparator_9 (.a(Instruction[31:25]), .b(7'b0000001), .eq(b0000001));  // open: gt, lt
  Comparator #(.width(7)) comparator_10 (.a(Instruction[31:25]), .b(7'b0100000), .eq(b0100000));  // open: gt, lt
  Comparator #(.width(7)) comparator_11 (.a(Instruction[6:0]), .b(7'b1100111), .eq(comparator_11_eq));  // open: gt, lt
  Comparator #(.width(3)) comparator_12 (.a(Instruction[14:12]), .b(3'b000), .eq(comparator_12_eq));  // open: gt, lt
  Demultiplexer #(.enable("false"), .select(3)) demultiplexer_1 (
    .out0(p0), .out1(p1), .out2(p2), .out3(p3), .out4(p4), .out5(p5), .out6(p6), .out7(p7),
    .in(comparator_1_eq), .sel(Instruction[14:12]));
  and and_1 (jalr, comparator_11_eq, comparator_12_eq);
  Demultiplexer #(.enable("false"), .select(3)) demultiplexer_2 (
    .out0(lb), .out1(lh), .out2(lw), .in(LOAD), .sel(Instruction[14:12]));  // open: out3, out4, out5, out6, out7
  Demultiplexer #(.enable("false"), .select(3)) demultiplexer_3 (
    .out0(addi), .out1(demultiplexer_3_out1), .out2(slti), .out4(xori), .out5(demultiplexer_3_out5),
    .out6(ori), .out7(andi), .in(IMM), .sel(Instruction[14:12]));  // open: out3
  Demultiplexer #(.enable("false"), .select(3)) demultiplexer_4 (
    .out0(sb), .out1(sh), .out2(sw), .in(STORE), .sel(Instruction[14:12]));  // open: out3, out4, out5, out6, out7
  Demultiplexer #(.enable("false"), .select(3)) demultiplexer_5 (
    .out0(beq), .out1(bne), .out4(blt), .out5(bge), .out6(bltu), .out7(bgeu), .in(JMP),
    .sel(Instruction[14:12]));  // open: out2, out3
  not not_1 (not_1_out, BrEq);
  Comparator #(.width(7)) comparator_13 (.a(Instruction[31:25]), .b({7{1'b0}}), .eq(b0000000));  // open: gt, lt
  or or_1 (PCSel, c7, c1, c2, c3, c4, c5, c6, c8);
  and and_2 (c1, beq, BrEq);
  and and_3 (c2, bne, not_1_out);
  and and_4 (c3, blt, BrLt);
  and and_5 (slli, b0000000, demultiplexer_3_out1);
  and and_6 (add, b0000000, p0);
  and and_7 (mul, b0000001, p0);
  and and_8 (sub, b0100000, p0);
  and and_9 (sll3, b0000000, p1);
  and and_10 (srli, b0000000, demultiplexer_3_out5);
  and and_11 (srai, demultiplexer_3_out5, b0100000);
  and and_12 (mulh, b0000001, p1);
  and and_13 (mulhu, b0000001, p3);
  not not_2 (not_2_out, BrLt);
  not not_3 (not_3_out, BrLt);
  and and_14 (slt, b0000000, p2);
  and and_15 (xor7, b0000000, p4);
  Comparator #(.width(7)) comparator_14 (.a(Instruction[6:0]), .b(7'b1101111), .eq(c7));  // open: gt, lt
  Comparator #(.width(7)) comparator_15 (.a(Instruction[6:0]), .b(7'b1100111), .eq(c8));  // open: gt, lt
  or or_2 (or_2_out, not_2_out, BrEq);
  or or_3 (or_3_out, not_3_out, BrEq);
  and and_16 (c4, bge, or_2_out);
  and and_17 (c5, bltu, BrLt);
  and and_18 (c6, bgeu, or_3_out);
  and and_19 (srl8, b0000000, p5);
  and and_20 (sra9, b0100000, p5);
  and and_21 (or10, b0000000, p6);
  and and_22 (and11, b0000000, p7);
  Priority_Encoder #(.select(5)) priority_encoder_1 (
    .in0(add), .in1(mul), .in2(sub), .in3(sll3), .in4(mulh), .in5(mulhu), .in6(slt), .in7(xor7), .in8(srl8),
    .in9(sra9), .in10(or10), .in11(and11), .in12(lb), .in13(lh), .in14(lw), .in15(addi), .in16(slli),
    .in17(slti), .in18(xori), .in19(srli), .in20(srai), .in21(ori), .in22(andi), .in23(sb), .in24(sh),
    .in25(sw), .in26(beq), .in27(bne), .in28(blt), .in29(bge), .in30(bltu), .in31(bgeu),
    .out(priority_encoder_1_out), .en_out(priority_encoder_1_en_out[0]));  // open: gs, en_in
  Priority_Encoder priority_encoder_2 (
    .in0(auipc), .in1(lui), .in2(jal), .in3(jalr), .out(priority_encoder_2_out),
    .en_out(priority_encoder_1_en_out[1]));  // open: in4, in5, in6, in7, en_in, gs
  assign bit_extender_1_out = {{1{1'b0}}, priority_encoder_1_out};  // Bit_Extender bit_extender_1
  assign bit_extender_2_out = {{3{1'b0}}, priority_encoder_2_out};  // Bit_Extender bit_extender_2
  Adder #(.width(6)) adder_1 (.a(bit_extender_2_out), .b(6'b100000), .out(adder_1_out));  // open: cin, cout
  Multiplexer #(.enable("false"), .select(2), .width(6)) multiplexer_1 (
    .in1(adder_1_out), .in2(bit_extender_1_out), .in3({6{1'b1}}), .out(input0),
    .sel(priority_encoder_1_en_out));  // open: in0

  // Other names for the same wires on the sheet: opcode[6:0] = Instruction[6:0]; funct3[2:0] = Instruction[14:12];
  //   funct7[6:0] = Instruction[31:25]

  // Notes on the sheet:
  //   INPUTS to your circuit
  //   Connect ROM Input here ->
  //   contents of rom_1 (hex, n*v repeats v):
  //   1001 1401 1601 1081 1481 1581 1101 1201 1281 1681 1301 1381 41 41 41 1041 10c1 1141 1241 12c1 16c1
  //   1341 13c1 1842 1842 1842 4*1064 1074 1074 1067 1047 2069 2041
  //   ROM FOR CONTROL LOGIC
  //   DON'T CHANGE THE LOCATIONS OF THE INPUTS AND OUTPUTS!
  //   This is only if you choose to do the ROM option
  //   CONNECT
  //   WIRE
  //   TO
  //   USE
  //   ROM
  //   OUTPUT from your circuit
  //   Reminder: If using ROM, use combinational logic for PCSel
endmodule
