// Logisim project cpu.circ as structural Verilog: 1 circuit, main circuit cpu
module cpu (
  input  clk,
  input  [31:0] Instruction,
  input  [31:0] MemReadData,
  output [31:0] MemAddress,
  output [31:0] ProgramCounter,
  output [31:0] ra,
  output [31:0] sp,
  output [31:0] t0,
  output [31:0] t1,
  output [31:0] t2,
  output [31:0] s0,
  output [31:0] s1,
  output [31:0] a0,
  output [3:0] MemWriteMask,
  output [31:0] MemWriteData
);

  wire ASel, BrEq, BrLt, BrUn, BSel, comparator_1_eq, MemWEn, PCSel, REGWEn;
  wire [1:0] WBSel;
  wire [2:0] ImmSel;
  wire [3:0] ALUSel;
  wire [4:0] rs1;
  wire [31:0] Data1, Data2, Imm, Instruction1, MemData, multiplexer_1_out, multiplexer_3_out,
       multiplexer_4_out, multiplexer_5_out, PC, PC4, PCplus4, WriteBack;

  Multiplexer #(.enable("false"), .width(32)) multiplexer_1 (
    .in0(Instruction), .in1(32'h33), .out(multiplexer_1_out), .sel(PCSel));
  Comparator #(.width(7)) comparator_1 (.a(Instruction1[6:0]), .b(7'b0110111), .eq(comparator_1_eq));  // open: gt, lt
  Register #(.width(32)) register_1 (.D(multiplexer_1_out), .en(1'b1), .clk(clk), .Q(Instruction1));  // open: clr
  Multiplexer #(.enable("false"), .width(5)) multiplexer_2 (
    .in0(Instruction1[19:15]), .in1({5{1'b0}}), .out(rs1), .sel(comparator_1_eq));
  Multiplexer #(.enable("false"), .width(32)) multiplexer_3 (
    .in0(PC4), .in1(MemAddress), .out(multiplexer_3_out), .sel(PCSel));
  Register #(.width(32)) u_PC (.D(multiplexer_3_out), .en(1'b1), .clk(clk), .Q(ProgramCounter));  // open: clr
  Register #(.width(32)) register_2 (.D(ProgramCounter), .en(1'b1), .clk(clk), .Q(PC));  // open: clr
  control_logic control_logic_1 (
    .PCSel(PCSel), .RegWEn(REGWEn), .ImmSel(ImmSel), .BrUn(BrUn), .ASel(ASel), .BSel(BSel), .ALUSel(ALUSel),
    .MemWEn(MemWEn), .WBSel(WBSel), .Instruction(Instruction1), .BrEq(BrEq), .BrLt(BrLt));
  Adder #(.width(32)) adder_1 (.a(ProgramCounter), .b(32'h4), .out(PC4));  // open: cin, cout
  regfile regfile_1 (
    .ReadReg1(rs1), .ReadReg2(Instruction1[24:20]), .WriteReg(Instruction1[11:7]), .RegWriteData(WriteBack),
    .RegWEn(REGWEn), .clk(clk), .ra(ra), .sp(sp), .t0(t0), .t1(t1), .t2(t2), .s0(s0), .s1(s1), .a0(a0),
    .RegReadData1(Data1), .RegReadData2(Data2));
  imm_gen imm_gen_1 (.Instruction(Instruction1), .ImmSel(ImmSel), .Immediate(Imm));
  Adder #(.width(32)) adder_2 (.a(PC), .b(32'h4), .out(PCplus4));  // open: cin, cout
  Multiplexer #(.enable("false"), .width(32)) multiplexer_4 (
    .in0(Data1), .in1(PC), .out(multiplexer_4_out), .sel(ASel));
  Multiplexer #(.enable("false"), .width(32)) multiplexer_5 (
    .in0(Data2), .in1(Imm), .out(multiplexer_5_out), .sel(BSel));
  alu alu_1 (.ALUResult(MemAddress), .A(multiplexer_4_out), .B(multiplexer_5_out), .ALUSel(ALUSel));
  branch_comp branch_comp_1 (.BrData1(Data1), .BrData2(Data2), .BrUn(BrUn), .BrEq(BrEq), .BrLt(BrLt));
  Multiplexer #(.enable("false"), .select(2), .width(32)) multiplexer_6 (
    .in0(MemData), .in1(MemAddress), .in2(PCplus4), .out(WriteBack), .sel(WBSel));  // open: in3
  partial_store partial_store_1 (
    .Instruction(Instruction1), .MemAddress(MemAddress), .DataFromReg(Data2), .MemWEn(MemWEn),
    .MemWriteMask(MemWriteMask), .DataToMem(MemWriteData));
  partial_load partial_load_1 (
    .Instruction(Instruction1), .MemAddress(MemAddress), .DataFromMem(MemReadData), .DataToReg(MemData));

  // Other names for the same wires on the sheet: rd[4:0] = Instruction1[11:7]; rs2[4:0] = Instruction1[24:20];
  //   Result[31:0] = MemAddress

  // Notes on the sheet:
  //   To IMEM
  //   IMEM (do **NOT** move this)
  //   From IMEM
  //   Inputs/Outputs for testing. Do **NOT** move these.
  //   It is OK to move the PC, RegFile, ALU, MEM, Branch Comp, Imm Gen, Partial Load, Partial Store and Control Logic to wherever is most convenient for you when constructing your CPU, and to delete this text
  //   To DMEM
  //   DMEM (do **NOT** move this)
  //   From DMEM
endmodule
