// Logisim project regfile.circ as structural Verilog: 1 circuit, main circuit regfile
module regfile (
  input  [4:0] ReadReg1,
  input  [4:0] ReadReg2,
  input  [4:0] WriteReg,
  input  [31:0] RegWriteData,
  input  RegWEn,
  input  clk,
  output [31:0] ra,
  output [31:0] sp,
  output [31:0] t0,
  output [31:0] t1,
  output [31:0] t2,
  output [31:0] s0,
  output [31:0] s1,
  output [31:0] a0,
  output [31:0] RegReadData1,
  output [31:0] RegReadData2
);

  wire P1, P2, P3, P4, P5, P6, P7, P8, P9, P10, P11, P12, P13, P14, P15, P16, P17, P18, P19, P20, P21, P22,
       P23, P24, P25, P26, P27, P28, P29, P30, P31, P32;
  wire [31:0] a1, a2, a3, a4, a5, a6, a7, gp, s2, s3, s4, s5, s6, s7, s8, s9, s10, s11, t3, t4, t5, t6, tp,
       zero;

  Demultiplexer #(.enable("false"), .select(5)) demultiplexer_1 (
    .out0(P1), .out1(P2), .out2(P3), .out3(P4), .out4(P5), .out5(P6), .out6(P7), .out7(P8), .out8(P9),
    .out9(P10), .out10(P11), .out11(P12), .out12(P13), .out13(P14), .out14(P15), .out15(P16), .out16(P17),
    .out17(P18), .out18(P19), .out19(P20), .out20(P21), .out21(P22), .out22(P23), .out23(P24), .out24(P25),
    .out25(P26), .out26(P27), .out27(P28), .out28(P29), .out29(P30), .out30(P31), .out31(P32), .in(RegWEn),
    .sel(WriteReg));
  Register #(.width(32)) register_1 (.D({32{1'b0}}), .clk(clk), .Q(zero));  // open: en, clr
  Register #(.width(32)) register_2 (.D(RegWriteData), .en(P2), .clk(clk), .Q(ra));  // open: clr
  Register #(.width(32)) register_3 (.D(RegWriteData), .en(P3), .clk(clk), .Q(sp));  // open: clr
  Register #(.width(32)) register_4 (.D(RegWriteData), .en(P4), .clk(clk), .Q(gp));  // open: clr
  Register #(.width(32)) register_5 (.D(RegWriteData), .en(P5), .clk(clk), .Q(tp));  // open: clr
  Register #(.width(32)) register_6 (.D(RegWriteData), .en(P6), .clk(clk), .Q(t0));  // open: clr
  Register #(.width(32)) register_7 (.D(RegWriteData), .en(P7), .clk(clk), .Q(t1));  // open: clr
  Register #(.width(32)) register_8 (.D(RegWriteData), .en(P8), .clk(clk), .Q(t2));  // open: clr
  Multiplexer #(.enable("false"), .select(5), .width(32)) multiplexer_1 (
    .in0(zero), .in1(ra), .in2(sp), .in3(gp), .in4(tp), .in5(t0), .in6(t1), .in7(t2), .in8(s0), .in9(s1),
    .in10(a0), .in11(a1), .in12(a2), .in13(a3), .in14(a4), .in15(a5), .in16(a6), .in17(a7), .in18(s2),
    .in19(s3), .in20(s4), .in21(s5), .in22(s6), .in23(s7), .in24(s8), .in25(s9), .in26(s10), .in27(s11),
    .in28(t3), .in29(t4), .in30(t5), .in31(t6), .out(RegReadData1), .sel(ReadReg1));
  Register #(.width(32)) register_9 (.D(RegWriteData), .en(P9), .clk(clk), .Q(s0));  // open: clr
  Register #(.width(32)) register_10 (.D(RegWriteData), .en(P16), .clk(clk), .Q(a5));  // open: clr
  Register #(.width(32)) register_11 (.D(RegWriteData), .en(P10), .clk(clk), .Q(s1));  // open: clr
  Register #(.width(32)) register_12 (.D(RegWriteData), .en(P11), .clk(clk), .Q(a0));  // open: clr
  Register #(.width(32)) register_13 (.D(RegWriteData), .en(P12), .clk(clk), .Q(a1));  // open: clr
  Register #(.width(32)) register_14 (.D(RegWriteData), .en(P13), .clk(clk), .Q(a2));  // open: clr
  Register #(.width(32)) register_15 (.D(RegWriteData), .en(P14), .clk(clk), .Q(a3));  // open: clr
  Register #(.width(32)) register_16 (.D(RegWriteData), .en(P15), .clk(clk), .Q(a4));  // open: clr
  Multiplexer #(.enable("false"), .select(5), .width(32)) multiplexer_2 (
    .in0(zero), .in1(ra), .in2(sp), .in3(gp), .in4(tp), .in5(t0), .in6(t1), .in7(t2), .in8(s0), .in9(s1),
    .in10(a0), .in11(a1), .in12(a2), .in13(a3), .in14(a4), .in15(a5), .in16(a6), .in17(a7), .in18(s2),
    .in19(s3), .in20(s4), .in21(s5), .in22(s6), .in23(s7), .in24(s8), .in25(s9), .in26(s10), .in27(s11),
    .in28(t3), .in29(t4), .in30(t5), .in31(t6), .out(RegReadData2), .sel(ReadReg2));
  Register #(.width(32)) register_17 (.D(RegWriteData), .en(P17), .clk(clk), .Q(a6));  // open: clr
  Register #(.width(32)) register_18 (.D(RegWriteData), .en(P18), .clk(clk), .Q(a7));  // open: clr
  Register #(.width(32)) register_19 (.D(RegWriteData), .en(P19), .clk(clk), .Q(s2));  // open: clr
  Register #(.width(32)) register_20 (.D(RegWriteData), .en(P20), .clk(clk), .Q(s3));  // open: clr
  Register #(.width(32)) register_21 (.D(RegWriteData), .en(P21), .clk(clk), .Q(s4));  // open: clr
  Register #(.width(32)) register_22 (.D(RegWriteData), .en(P22), .clk(clk), .Q(s5));  // open: clr
  Register #(.width(32)) register_23 (.D(RegWriteData), .en(P23), .clk(clk), .Q(s6));  // open: clr
  Register #(.width(32)) register_24 (.D(RegWriteData), .en(P24), .clk(clk), .Q(s7));  // open: clr
  Register #(.width(32)) register_25 (.D(RegWriteData), .en(P25), .clk(clk), .Q(s8));  // open: clr
  Register #(.width(32)) register_26 (.D(RegWriteData), .en(P26), .clk(clk), .Q(s9));  // open: clr
  Register #(.width(32)) register_27 (.D(RegWriteData), .en(P27), .clk(clk), .Q(s10));  // open: clr
  Register #(.width(32)) register_28 (.D(RegWriteData), .en(P28), .clk(clk), .Q(s11));  // open: clr
  Register #(.width(32)) register_29 (.D(RegWriteData), .en(P29), .clk(clk), .Q(t3));  // open: clr
  Register #(.width(32)) register_30 (.D(RegWriteData), .en(P30), .clk(clk), .Q(t4));  // open: clr
  Register #(.width(32)) register_31 (.D(RegWriteData), .en(P31), .clk(clk), .Q(t5));  // open: clr
  Register #(.width(32)) register_32 (.D(RegWriteData), .en(P32), .clk(clk), .Q(t6));  // open: clr

  // Other names for the same wires on the sheet: fp[31:0] = s0

  // Notes on the sheet:
  //   INPUTS to your circuit
  //   DON'T CHANGE THE LOCATIONS OF THE INPUTS AND OUTPUTS!
  //   These are DEBUG/TEST outputs from your circuit.
  //   OUTPUTS from your circuit
endmodule
